# Fritzing sketch RX module (saved by Fritzing 0.9.3b)
breadboards: 1

parts:
  part = Adafruit Feather 32u4 RFM9xW LoRa
  868MHz_antenna = Antenna

nets:
  N1: part.ANT, 868MHz_antenna.antenna_lead
  S.Bus: part.1
  GND: part.GND
  +5V: part.VBUS

custom parts:
  Adafruit Feather 32u4 RFM9xW LoRa: This is the Adafruit Feather 32u4 LoRa Radio (RFM9x) - our take on an microcontroller with a "Long Range (LoRa)" packet radio transceiver with built in USB and battery charging. Its an Adafruit Feather 32u4 with a 868/915 MHz radio module cooked in! Great for making wireless networks that can go further than 2.4GHz 802.15.4 and similar, are more flexible than Bluetooth LE and without the high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
